# Fritzing sketch rampart (saved by Fritzing 0.9.3b)
circuit board: 8.46667cm x 5.64444cm
breadboards: 1

parts:
  Part1 = Arduino Nano (Rev3.0)
  R1 = Rotary Potentiometer (Small) [maximum_resistance=100kΩ package=THT]
  J1 = Piezo Speaker
  10K = Rotary Potentiometer (Small) [maximum_resistance=100kΩ package=THT]
  R4 = Rotary Potentiometer (Small) [maximum_resistance=100kΩ package=THT]
  J2 = female pin header, 4 pins [form="♀ (female)"]
  S2 = Pushbutton [package="[SMD]"]
  S3 = Pushbutton [package="[SMD]"]
  R3 = Rotary Potentiometer (Small) [maximum_resistance=100kΩ package=THT]
  R5 = Resistor [tolerance=±5% resistance=10k package=THT]
  R6 = Resistor [tolerance=±5% resistance=10k package=THT]

nets (from the pcb view):
  N1: Part1.GND, R1.leg1, J1.pin1, 10K.leg1, R4.leg1, R3.leg1, R5.Pin_0, R6.Pin_0
  N2: Part1.D2, Part1.5V, R1.leg2, 10K.leg2, R4.leg2, S2.Pin_1, S2.Pin_2, S3.Pin_3, S3.Pin_4, R3.leg2, R5.Pin_1
  N3: Part1.D3, S2.Pin_3, S2.Pin_4, R6.Pin_1
  N4: Part1.D9, J1.pin2
  N5: Part1.A7, J2.pin4
  N6: Part1.A6, J2.pin3
  N7: Part1.A5, J2.pin2
  N8: Part1.A4, J2.pin1
  N9: Part1.A3, 10K.wiper
  N10: Part1.A2, R3.wiper
  N11: Part1.A1, R4.wiper
  N12: Part1.A0, R1.wiper
  N13: S3.Pin_1, S3.Pin_2
